// Logisim project noughts_and_crosses.circ as structural Verilog: 10 circuits, main circuit main
module main (
  input  Enable_hard_level
);

  wire cdm_8_1_p2, cdm_8_1_p4, cdm_8_1_p5, cdm_8_1_p6, cdm_8_1_p7, cdm_8_1_p8, cdm_8_1_p9, clock, code, data,
       game_controller_1_draw, game_controller_1_move, game_controller_1_switch_move, game_controller_1_win,
       I_O, I_Osel, in0, in1, in2, in3, in4, in5, in6, in7, in8, mem, move_getter_1_move, nand_1_out,
       not_1_out, not_2_out, not_3_out, not_4_out, RAM, reset, switch_move;
  wire [1:0] dis0, dis1, dis2, dis3, dis4, dis5, dis6, dis7, dis8;
  wire [2:0] display_controller_1_out_2, display_controller_1_out_3, display_controller_1_out_4,
       display_controller_2_out_2, display_controller_2_out_3, display_controller_2_out_4,
       display_controller_3_out_2, display_controller_3_out_3, display_controller_3_out_4,
       display_controller_4_out_2, display_controller_4_out_3, display_controller_4_out_4,
       display_controller_5_out_2, display_controller_5_out_3, display_controller_5_out_4,
       display_controller_6_out_2, display_controller_6_out_3, display_controller_6_out_4,
       display_controller_7_out_2, display_controller_7_out_3, display_controller_7_out_4,
       display_controller_8_out_2, display_controller_8_out_3, display_controller_8_out_4,
       display_controller_9_out_2, display_controller_9_out_3, display_controller_9_out_4;
  wire [5:0] scoreboard_controller_1__0, scoreboard_controller_1__1, scoreboard_controller_1_out_8,
       scoreboard_controller_1_out_9, scoreboard_controller_1_out_10, scoreboard_controller_1_out_11,
       scoreboard_controller_1_out_12, scoreboard_controller_1_out_13, scoreboard_controller_1_out_14,
       scoreboard_controller_1_out_15, scoreboard_controller_1_out_16, scoreboard_controller_1_out_17,
       scoreboard_controller_1_out_18, scoreboard_controller_1_out_19, scoreboard_controller_1_out_20,
       scoreboard_controller_1_out_21, scoreboard_controller_1_out_22, scoreboard_controller_1_out_23,
       scoreboard_controller_1_out_24, scoreboard_controller_1_out_25, scoreboard_controller_1_out_26,
       scoreboard_controller_1_out_27, scoreboard_controller_1_out_28, scoreboard_controller_1_out_29,
       scoreboard_controller_1_out_30, scoreboard_controller_1_out_31, scoreboard_controller_1_out_32,
       scoreboard_controller_1_out_33, scoreboard_controller_1_out_34, scoreboard_controller_1_out_35,
       scoreboard_controller_1_out_36, scoreboard_controller_1_out_37;
  wire [7:0] cdm_8_1_p13, cdm_8_1_p14, demultiplexer_1_out0, demultiplexer_1_out1, I_Oadr, I_Odat,
       move_getter_1_data, rom_1_data, rom_2_data;
  wire [7:4] cdm_8_1_p12;
  wire [23:0] game_bus;

  // Probe on cdm_8_1_p2
  Clock clock_1 (.out(clock));
  // Probe on cdm_8_1_p5
  // Probe on cdm_8_1_p6
  // Probe on cdm_8_1_p4
  // Probe on cdm_8_1_p7
  and and_1 (I_Osel, not_1_out, clock, data);
  // Probe on cdm_8_1_p8
  not not_1 (not_1_out, nand_1_out);
  and and_2 (RAM, nand_1_out, data);
  byte_selector byte_selector_1 (.game_bus(game_bus), .I_Oadr(I_Oadr), .I_Osel(I_Osel), .I_O(I_O), .data(I_Odat));
  // CdM_8 cdm_8_1: pin names not known; wires that end beside it: clock, cdm_8_1_p2, switch_move, cdm_8_1_p4, cdm_8_1_p5, cdm_8_1_p6, cdm_8_1_p7, cdm_8_1_p8, cdm_8_1_p9, mem, I_O, {cdm_8_1_p12, I_Oadr[3:0]}, cdm_8_1_p13, cdm_8_1_p14
  nand nand_1 (nand_1_out, not_3_out, cdm_8_1_p12[5], cdm_8_1_p12[6], cdm_8_1_p12[7]);
  move_getter move_getter_1 (
    .I_Odata(I_Odat), .I_Osel(I_Osel), .I_O(I_O), .data(move_getter_1_data), .move(move_getter_1_move));
  Pull_Resistor pull_resistor_1 (.node(code));
  Pull_Resistor pull_resistor_2 (.node(data));
  Decoder decoder_1 (.out0(code), .out1(data), .sel(cdm_8_1_p9), .en(mem));
  assign I_Odat = not_2_out ? cdm_8_1_p13 : 8'bz;  // Controlled_Buffer controlled_buffer_1
  not not_2 (not_2_out, I_O);
  assign cdm_8_1_p14 = I_O ? I_Odat : 8'bz;  // Controlled_Buffer controlled_buffer_2
  not not_3 (not_3_out, cdm_8_1_p12[4]);
  Demultiplexer #(.width(8), .enable("false")) demultiplexer_1 (
    .out0(demultiplexer_1_out0), .out1(demultiplexer_1_out1), .in({cdm_8_1_p12, I_Oadr[3:0]}),
    .sel(Enable_hard_level));
  Pull_Resistor pull_resistor_3 (.node(I_Oadr[0]));
  Pull_Resistor pull_resistor_4 (.node(I_Oadr[1]));
  Pull_Resistor pull_resistor_5 (.node(I_Oadr[2]));
  Pull_Resistor pull_resistor_6 (.node(I_Oadr[3]));
  Pull_Resistor pull_resistor_7 (.node(cdm_8_1_p12[4]));
  Pull_Resistor pull_resistor_8 (.node(cdm_8_1_p12[5]));
  Pull_Resistor pull_resistor_9 (.node(cdm_8_1_p12[6]));
  Pull_Resistor pull_resistor_10 (.node(cdm_8_1_p12[7]));
  and and_3 (switch_move, not_4_out, game_controller_1_switch_move);
  not not_4 (not_4_out, game_controller_1_move);
  game_controller game_controller_1 (
    .in0(in0), .in1(in1), .in2(in2), .in3(in3), .in4(in4), .in5(in5), .in6(in6), .in7(in7), .in8(in8),
    .Out(game_bus), .switch_move(game_controller_1_switch_move), .move(game_controller_1_move),
    .win(game_controller_1_win), .draw(game_controller_1_draw), .comp_move(move_getter_1_move),
    .comp_value(move_getter_1_data), .Reset(reset));
  Button R (.out(reset));
  ROM rom_1 (.addr(demultiplexer_1_out0), .data(rom_1_data), .sel(code));
  ROM rom_2 (.addr(demultiplexer_1_out1), .data(rom_2_data), .sel(code));
  RAM ram_1 (.addr({cdm_8_1_p12, I_Oadr[3:0]}), .data(I_Odat), .sel(RAM), .clk(clock), .ld(I_O));  // open: clr
  game_bus_div game_bus_div_1 (
    .in_1(game_bus), .out_2(dis0), .out_3(dis1), .out_4(dis2), .out_5(dis3), .out_6(dis4), .out_7(dis5),
    .out_8(dis6), .out_9(dis7), .out_10(dis8));
  Multiplexer #(.width(8), .enable("false")) multiplexer_1 (
    .in0(rom_1_data), .in1(rom_2_data), .out(I_Odat), .sel(Enable_hard_level));
  DotMatrix #(.matrixcols(32), .matrixrows(6)) dotmatrix_1 (
    .col0(scoreboard_controller_1__0), .col1(scoreboard_controller_1__1),
    .col2(scoreboard_controller_1_out_8), .col3(scoreboard_controller_1_out_9),
    .col4(scoreboard_controller_1_out_10), .col5(scoreboard_controller_1_out_11),
    .col6(scoreboard_controller_1_out_12), .col7(scoreboard_controller_1_out_13),
    .col8(scoreboard_controller_1_out_14), .col9(scoreboard_controller_1_out_15),
    .col10(scoreboard_controller_1_out_16), .col11(scoreboard_controller_1_out_17),
    .col12(scoreboard_controller_1_out_18), .col13(scoreboard_controller_1_out_19),
    .col14(scoreboard_controller_1_out_20), .col15(scoreboard_controller_1_out_21),
    .col16(scoreboard_controller_1_out_22), .col17(scoreboard_controller_1_out_23),
    .col18(scoreboard_controller_1_out_24), .col19(scoreboard_controller_1_out_25),
    .col20(scoreboard_controller_1_out_26), .col21(scoreboard_controller_1_out_27),
    .col22(scoreboard_controller_1_out_28), .col23(scoreboard_controller_1_out_29),
    .col24(scoreboard_controller_1_out_30), .col25(scoreboard_controller_1_out_31),
    .col26(scoreboard_controller_1_out_32), .col27(scoreboard_controller_1_out_33),
    .col28(scoreboard_controller_1_out_34), .col29(scoreboard_controller_1_out_35),
    .col30(scoreboard_controller_1_out_36), .col31(scoreboard_controller_1_out_37));
  scoreboard_controller scoreboard_controller_1 (
    .move(game_controller_1_move), .win(game_controller_1_win), .draw(game_controller_1_draw), .clock(clock),
    .reset(reset), ._0(scoreboard_controller_1__0), ._1(scoreboard_controller_1__1),
    .out_8(scoreboard_controller_1_out_8), .out_9(scoreboard_controller_1_out_9),
    .out_10(scoreboard_controller_1_out_10), .out_11(scoreboard_controller_1_out_11),
    .out_12(scoreboard_controller_1_out_12), .out_13(scoreboard_controller_1_out_13),
    .out_14(scoreboard_controller_1_out_14), .out_15(scoreboard_controller_1_out_15),
    .out_16(scoreboard_controller_1_out_16), .out_17(scoreboard_controller_1_out_17),
    .out_18(scoreboard_controller_1_out_18), .out_19(scoreboard_controller_1_out_19),
    .out_20(scoreboard_controller_1_out_20), .out_21(scoreboard_controller_1_out_21),
    .out_22(scoreboard_controller_1_out_22), .out_23(scoreboard_controller_1_out_23),
    .out_24(scoreboard_controller_1_out_24), .out_25(scoreboard_controller_1_out_25),
    .out_26(scoreboard_controller_1_out_26), .out_27(scoreboard_controller_1_out_27),
    .out_28(scoreboard_controller_1_out_28), .out_29(scoreboard_controller_1_out_29),
    .out_30(scoreboard_controller_1_out_30), .out_31(scoreboard_controller_1_out_31),
    .out_32(scoreboard_controller_1_out_32), .out_33(scoreboard_controller_1_out_33),
    .out_34(scoreboard_controller_1_out_34), .out_35(scoreboard_controller_1_out_35),
    .out_36(scoreboard_controller_1_out_36), .out_37(scoreboard_controller_1_out_37));
  Button button_1 (.out(in0));
  Button button_2 (.out(in3));
  Button button_3 (.out(in6));
  display_controller display_controller_1 (
    .in_1(dis0), .out_2(display_controller_1_out_2), .out_3(display_controller_1_out_3),
    .out_4(display_controller_1_out_4));
  DotMatrix #(.matrixcols(3), .matrixrows(3)) dotmatrix_2 (
    .col0(display_controller_1_out_2), .col1(display_controller_1_out_3), .col2(display_controller_1_out_4));
  DotMatrix #(.matrixcols(3), .matrixrows(3)) dotmatrix_3 (
    .col0(display_controller_2_out_2), .col1(display_controller_2_out_3), .col2(display_controller_2_out_4));
  display_controller display_controller_2 (
    .in_1(dis3), .out_2(display_controller_2_out_2), .out_3(display_controller_2_out_3),
    .out_4(display_controller_2_out_4));
  DotMatrix #(.matrixcols(3), .matrixrows(3)) dotmatrix_4 (
    .col0(display_controller_3_out_2), .col1(display_controller_3_out_3), .col2(display_controller_3_out_4));
  display_controller display_controller_3 (
    .in_1(dis6), .out_2(display_controller_3_out_2), .out_3(display_controller_3_out_3),
    .out_4(display_controller_3_out_4));
  DotMatrix #(.matrixcols(3), .matrixrows(3)) dotmatrix_5 (
    .col0(display_controller_4_out_2), .col1(display_controller_4_out_3), .col2(display_controller_4_out_4));
  display_controller display_controller_4 (
    .in_1(dis1), .out_2(display_controller_4_out_2), .out_3(display_controller_4_out_3),
    .out_4(display_controller_4_out_4));
  Button button_4 (.out(in1));
  display_controller display_controller_5 (
    .in_1(dis4), .out_2(display_controller_5_out_2), .out_3(display_controller_5_out_3),
    .out_4(display_controller_5_out_4));
  DotMatrix #(.matrixcols(3), .matrixrows(3)) dotmatrix_6 (
    .col0(display_controller_5_out_2), .col1(display_controller_5_out_3), .col2(display_controller_5_out_4));
  Button button_5 (.out(in4));
  display_controller display_controller_6 (
    .in_1(dis7), .out_2(display_controller_6_out_2), .out_3(display_controller_6_out_3),
    .out_4(display_controller_6_out_4));
  DotMatrix #(.matrixcols(3), .matrixrows(3)) dotmatrix_7 (
    .col0(display_controller_6_out_2), .col1(display_controller_6_out_3), .col2(display_controller_6_out_4));
  Button button_6 (.out(in7));
  DotMatrix #(.matrixcols(3), .matrixrows(3)) dotmatrix_8 (
    .col0(display_controller_7_out_2), .col1(display_controller_7_out_3), .col2(display_controller_7_out_4));
  display_controller display_controller_7 (
    .in_1(dis2), .out_2(display_controller_7_out_2), .out_3(display_controller_7_out_3),
    .out_4(display_controller_7_out_4));
  Button button_7 (.out(in2));
  DotMatrix #(.matrixcols(3), .matrixrows(3)) dotmatrix_9 (
    .col0(display_controller_8_out_2), .col1(display_controller_8_out_3), .col2(display_controller_8_out_4));
  display_controller display_controller_8 (
    .in_1(dis5), .out_2(display_controller_8_out_2), .out_3(display_controller_8_out_3),
    .out_4(display_controller_8_out_4));
  Button button_8 (.out(in5));
  DotMatrix #(.matrixcols(3), .matrixrows(3)) dotmatrix_10 (
    .col0(display_controller_9_out_2), .col1(display_controller_9_out_3), .col2(display_controller_9_out_4));
  display_controller display_controller_9 (
    .in_1(dis8), .out_2(display_controller_9_out_2), .out_3(display_controller_9_out_3),
    .out_4(display_controller_9_out_4));
  Button button_9 (.out(in8));

  // Other names for the same wires on the sheet: hl = Enable_hard_level; rd_wr = I_O

  // Notes on the sheet:
  //   INPUT chip
  //   I/O controller
  //   OUTPUT chip
  //   0xE
  //   Restart
  //   contents of rom_1 (hex, n*v repeats v):
  //   d1 0 d2 1 d3 2 d6 52 d1 3 d2 4 d3 5 d6 52 d1 6 d2 7 d3 8 d6 52 d1 0 d2 3 d3 6 d6 52 d1 1 d2 4 d3 7
  //   d6 52 d1 2 d2 5 d3 8 d6 52 d1 0 d2 4 d3 8 d6 52 d1 2 d2 4 d3 6 d6 52 d3 9 8b d0 e0 1c b0 0 e1 4e d0
  //   e9 a3 d4 f e1 42 d4 d0 e0 14 b0 51 d0 e0 18 b0 52 d0 e0 1c b0 53 d0 0 a1 8c a2 8c a3 d0 0 d2 3 d3 40
  //   8a b9 4d e0 74 8c a e1 6e d1 2 71 e1 8c d2 3 8a b9 d3 c0 47 e1 89 d2 e9 a9 d4 a e1 7e d7 d4
  //   contents of rom_2 (hex, n*v repeats v):
  //   d1 0 d2 1 d3 2 d6 52 d1 3 d2 4 d3 5 d6 52 d1 6 d2 7 d3 8 d6 52 d1 0 d2 3 d3 6 d6 52 d1 1 d2 4 d3 7
  //   d6 52 d1 2 d2 5 d3 8 d6 52 d1 0 d2 4 d3 8 d6 52 d1 2 d2 4 d3 6 d6 52 d3 9 8b d0 e0 1c b0 0 e1 4e d0
  //   e9 a3 d4 f e1 42 d4 d0 e0 14 b0 51 d0 e0 18 b0 52 d0 e0 1c b0 53 d0 0 a1 8c a2 8c a3 d0 0 d2 3 d3 40
  //   8a b9 4d e0 74 8c a e1 6e d1 2 71 e1 8c d2 3 8a b9 d3 c0 47 e1 89 d2 e9 a9 d4 a e1 7e d7 d4
  //   RAM
  //   ROM0/1 switcher
  //   ROM0
  //   ROM1
endmodule

module display_controller (
  input  [1:0] in_1,
  output [2:0] out_2,
  output [2:0] out_3,
  output [2:0] out_4
);

  wire not_1_out;
  wire [8:0] multiplexer_1_out;

  Multiplexer #(.width(9), .enable("false")) multiplexer_1 (
    .in0(9'h1ef), .in1(9'h155), .out(multiplexer_1_out), .sel(in_1[0]));
  not not_1 (not_1_out, in_1[1]);
  Multiplexer #(.width(9), .enable("false")) multiplexer_2 (
    .in0(multiplexer_1_out), .in1({9{1'b0}}), .out({out_4, out_3, out_2}), .sel(not_1_out));
endmodule

module game_bus_div (
  input  [23:0] in_1,
  output [1:0] out_2,
  output [1:0] out_3,
  output [1:0] out_4,
  output [1:0] out_5,
  output [1:0] out_6,
  output [1:0] out_7,
  output [1:0] out_8,
  output [1:0] out_9,
  output [1:0] out_10
);


  assign out_2 = in_1[23:22];
  assign out_3 = in_1[21:20];
  assign out_4 = in_1[19:18];
  assign out_5 = in_1[17:16];
  assign out_6 = in_1[15:14];
  assign out_7 = in_1[13:12];
  assign out_8 = in_1[11:10];
  assign out_9 = in_1[9:8];
  assign out_10 = in_1[7:6];
endmodule

module game_controller (
  input  in0,
  input  in1,
  input  in2,
  input  in3,
  input  in4,
  input  in5,
  input  in6,
  input  Reset,
  input  in7,
  input  in8,
  input  comp_move,
  input  [7:0] comp_value,
  output [23:0] Out,
  output move,
  output win,
  output draw,
  output switch_move
);

  wire and_2_out, com0, com1, com2, com3, com4, com5, com6, com7, com8, m, not_1_out, not_2_out, not_3_out,
       switch_move0, switch_move1, switch_move2, switch_move3, switch_move4, switch_move5, switch_move6,
       switch_move7, switch_move8, win_detector_1_win, win_detector_2_win, win_detector_3_win,
       win_detector_4_win, win_detector_5_win, win_detector_6_win, win_detector_7_win, win_detector_8_win;

  register_chip register_chip_1 (
    .player_in(in0), .computer_in(com0), ._0(Out[23]), ._1(Out[22]), .move_switch(switch_move0), .move(m),
    .win(win), .reset(Reset));
  register_chip register_chip_2 (
    .player_in(in1), .computer_in(com1), ._0(Out[21]), ._1(Out[20]), .move_switch(switch_move1), .move(m),
    .win(win), .reset(Reset));
  register_chip register_chip_3 (
    .player_in(in2), .computer_in(com2), ._0(Out[19]), ._1(Out[18]), .move_switch(switch_move2), .move(m),
    .win(win), .reset(Reset));
  register_chip register_chip_4 (
    .player_in(in3), .computer_in(com3), ._0(Out[17]), ._1(Out[16]), .move_switch(switch_move3), .move(m),
    .win(win), .reset(Reset));
  register_chip register_chip_5 (
    .player_in(in4), .computer_in(com4), ._0(Out[15]), ._1(Out[14]), .move_switch(switch_move4), .move(m),
    .win(win), .reset(Reset));
  register_chip register_chip_6 (
    .player_in(in5), .computer_in(com5), ._0(Out[13]), ._1(Out[12]), .move_switch(switch_move5), .move(m),
    .win(win), .reset(Reset));
  register_chip register_chip_7 (
    .player_in(in6), .computer_in(com6), ._0(Out[11]), ._1(Out[10]), .move_switch(switch_move6), .move(m),
    .win(win), .reset(Reset));
  register_chip register_chip_8 (
    .player_in(in7), .computer_in(com7), ._0(Out[9]), ._1(Out[8]), .move_switch(switch_move7), .move(m),
    .win(win), .reset(Reset));
  register_chip register_chip_9 (
    .player_in(in8), .computer_in(com8), ._0(Out[7]), ._1(Out[6]), .move_switch(switch_move8), .move(m),
    .win(win), .reset(Reset));
  Decoder #(.select(4)) decoder_1 (
    .out0(com0), .out1(com1), .out2(com2), .out3(com3), .out4(com4), .out5(com5), .out6(com6), .out7(com7),
    .out8(com8), .sel(comp_value[3:0]), .en(comp_move));  // open: out9, out10, out11, out12, out13, out14, out15
  Pull_Resistor pull_resistor_1 (.node(Out[5]));
  not not_1 (not_1_out, m);
  or or_1 (switch_move, switch_move0, switch_move1, switch_move2, switch_move3, switch_move4, switch_move5, switch_move6, switch_move7, switch_move8);
  win_detector win_detector_1 (
    ._0_active(Out[23]), ._0_status(Out[22]), ._1_active(Out[21]), ._1_status(Out[20]), ._2_active(Out[19]),
    ._2_status(Out[18]), .win(win_detector_1_win));
  win_detector win_detector_2 (
    ._0_active(Out[17]), ._0_status(Out[16]), ._1_active(Out[15]), ._1_status(Out[14]), ._2_active(Out[13]),
    ._2_status(Out[12]), .win(win_detector_2_win));
  win_detector win_detector_3 (
    ._0_active(Out[11]), ._0_status(Out[10]), ._1_active(Out[9]), ._1_status(Out[8]), ._2_active(Out[7]),
    ._2_status(Out[6]), .win(win_detector_3_win));
  win_detector win_detector_4 (
    ._0_active(Out[23]), ._0_status(Out[22]), ._1_active(Out[15]), ._1_status(Out[14]), ._2_active(Out[7]),
    ._2_status(Out[6]), .win(win_detector_4_win));
  Multiplexer #(.enable("false")) multiplexer_1 (.in0(m), .in1(not_2_out), .out(move), .sel(win));
  not not_2 (not_2_out, m);
  Register #(.width(1)) register_1 (.D(not_1_out), .Q(m), .clk(switch_move), .clr(Reset));  // open: en
  or or_2 (win, win_detector_4_win, win_detector_3_win, win_detector_2_win, win_detector_1_win, win_detector_5_win, win_detector_6_win, win_detector_7_win, win_detector_8_win);
  win_detector win_detector_5 (
    ._0_active(Out[11]), ._0_status(Out[10]), ._1_active(Out[17]), ._1_status(Out[16]), ._2_active(Out[23]),
    ._2_status(Out[22]), .win(win_detector_5_win));
  win_detector win_detector_6 (
    ._0_active(Out[9]), ._0_status(Out[8]), ._1_active(Out[15]), ._1_status(Out[14]), ._2_active(Out[21]),
    ._2_status(Out[20]), .win(win_detector_6_win));
  win_detector win_detector_7 (
    ._0_active(Out[7]), ._0_status(Out[6]), ._1_active(Out[13]), ._1_status(Out[12]), ._2_active(Out[19]),
    ._2_status(Out[18]), .win(win_detector_7_win));
  win_detector win_detector_8 (
    ._0_active(Out[11]), ._0_status(Out[10]), ._1_active(Out[15]), ._1_status(Out[14]), ._2_active(Out[19]),
    ._2_status(Out[18]), .win(win_detector_8_win));
  and and_1 (draw, not_3_out, and_2_out);
  not not_3 (not_3_out, win);
  and and_2 (and_2_out, Out[23], Out[21], Out[19], Out[17], Out[15], Out[13], Out[11], Out[9], Out[7]);

  assign Out[4:0] = {5{Out[5]}};

  // Other names for the same wires on the sheet: out8_1 = Out[6]; out8_0 = Out[7]; out7_1 = Out[8]; out7_0 = Out[9];
  //   out6_1 = Out[10]; out6_0 = Out[11]; out5_1 = Out[12]; out5_0 = Out[13]; out4_1 = Out[14]; out4_0 = Out[15];
  //   out3_1 = Out[16]; out3_0 = Out[17]; out2_1 = Out[18]; out2_0 = Out[19]; out1_1 = Out[20]; out1_0 = Out[21];
  //   out0_1 = Out[22]; out0_0 = Out[23]; r = Reset; w = win

  // Notes on the sheet:
  //   0 ---
  //   1 ---
  //   2 ---
  //   \
  //   0 |
  //   1 |
  //   2 |
  //   /
endmodule

// Reg
module register_chip (
  input  player_in,
  input  computer_in,
  input  move,
  input  win,
  input  reset,
  output _0,
  output _1,
  output move_switch
);

  wire and_1_out, and_2_out, and_3_out, not_1_out, not_2_out, not_3_out, or_1_out;
  wire [1:0] multiplexer_1_out;

  not not_1 (not_1_out, move);
  Pull_Resistor pull_resistor_1 (.node(computer_in));
  and and_1 (and_1_out, player_in, not_1_out);
  and and_2 (and_2_out, computer_in, move);
  or or_1 (or_1_out, and_1_out, and_2_out);
  and and_3 (and_3_out, or_1_out, not_2_out);
  not not_2 (not_2_out, win);
  Multiplexer #(.width(2), .enable("false")) multiplexer_1 (
    .in0(2'b11), .in1(2'b01), .out(multiplexer_1_out), .sel(move));
  Register #(.width(2)) register_1 (.D(multiplexer_1_out), .Q({_1, _0}), .clk(move_switch), .clr(reset));  // open: en
  not not_3 (not_3_out, _0);
  and and_4 (move_switch, not_3_out, and_3_out);
endmodule

// win_check
module win_detector (
  input  _0_active,
  input  _0_status,
  input  _1_active,
  input  _1_status,
  input  _2_active,
  input  _2_status,
  output win
);

  wire and_1_out, and_2_out, nor_1_out, or_1_out;

  and and_1 (and_1_out, _0_active, _1_active, _2_active);
  nor nor_1 (nor_1_out, _0_status, _1_status, _2_status);
  or or_1 (or_1_out, nor_1_out, and_2_out);
  and and_2 (and_2_out, _0_status, _1_status, _2_status);
  and and_3 (win, and_1_out, or_1_out);
endmodule

module scoreboard_controller (
  input  move,
  input  win,
  input  draw,
  input  clock,
  input  reset,
  output [5:0] _0,
  output [5:0] _1,
  output [5:0] out_8,
  output [5:0] out_9,
  output [5:0] out_10,
  output [5:0] out_11,
  output [5:0] out_12,
  output [5:0] out_13,
  output [5:0] out_14,
  output [5:0] out_15,
  output [5:0] out_16,
  output [5:0] out_17,
  output [5:0] out_18,
  output [5:0] out_19,
  output [5:0] out_20,
  output [5:0] out_21,
  output [5:0] out_22,
  output [5:0] out_23,
  output [5:0] out_24,
  output [5:0] out_25,
  output [5:0] out_26,
  output [5:0] out_27,
  output [5:0] out_28,
  output [5:0] out_29,
  output [5:0] out_30,
  output [5:0] out_31,
  output [5:0] out_32,
  output [5:0] out_33,
  output [5:0] out_34,
  output [5:0] out_35,
  output [5:0] out_36,
  output [5:0] out_37
);

  wire cl, comparator_1_eq, not_1_out, or_1_out;
  wire [3:0] counter_2_q;
  wire [4:0] counter_1_q;
  wire [5:0] multiplexer_1_out, multiplexer_2_out, rom_1_data, rom_2_data, rom_3_data;

  Counter #(.width(5), .max('h1f)) counter_1 (.Q(counter_1_q), .clk(cl), .clr(reset));  // open: load, D, count, carry
  Counter #(.width(4), .max('hf)) counter_2 (
    .Q(counter_2_q), .clk(clock), .clr(comparator_1_eq));  // open: load, D, count, carry
  not not_1 (not_1_out, move);
  or or_1 (or_1_out, win, draw);
  Comparator #(.width(4), .mode("unsigned")) comparator_1 (
    .a(counter_2_q), .b(4'b1111), .eq(comparator_1_eq));  // open: gt, lt
  ROM #(.addrWidth(5), .dataWidth(6)) rom_1 (.addr(counter_1_q), .data(rom_1_data), .sel(not_1_out));
  ROM #(.addrWidth(5), .dataWidth(6)) rom_2 (.addr(counter_1_q), .data(rom_2_data), .sel(move));
  ROM #(.addrWidth(5), .dataWidth(6)) rom_3 (.addr(counter_1_q), .data(rom_3_data), .sel(draw));
  and and_1 (cl, or_1_out, comparator_1_eq);
  Multiplexer #(.width(6), .enable("false")) multiplexer_1 (
    .in0(rom_1_data), .in1(rom_2_data), .out(multiplexer_1_out), .sel(move));
  Multiplexer #(.width(6), .enable("false")) multiplexer_2 (
    .in0(multiplexer_1_out), .in1(rom_3_data), .out(multiplexer_2_out), .sel(draw));
  Register #(.width(6)) register_1 (.D(_0), .Q(_1), .clk(cl), .clr(reset));  // open: en
  Register #(.width(6)) register_2 (.D(multiplexer_2_out), .Q(_0), .clk(cl), .clr(reset));  // open: en
  Register #(.width(6)) register_3 ();  // open: D, en, Q, clk, clr
  Register #(.width(6)) register_4 (.D(_1), .Q(out_8), .clk(cl), .clr(reset));  // open: en
  Register #(.width(6)) register_5 (.D(out_8), .Q(out_9), .clk(cl), .clr(reset));  // open: en
  Register #(.width(6)) register_6 (.D(out_9), .Q(out_10), .clk(cl), .clr(reset));  // open: en
  Register #(.width(6)) register_7 (.D(out_10), .Q(out_11), .clk(cl), .clr(reset));  // open: en
  Register #(.width(6)) register_8 (.D(out_11), .Q(out_12), .clk(cl), .clr(reset));  // open: en
  Register #(.width(6)) register_9 (.D(out_12), .Q(out_13), .clk(cl), .clr(reset));  // open: en
  Register #(.width(6)) register_10 (.D(out_14), .Q(out_15), .clk(cl), .clr(reset));  // open: en
  Register #(.width(6)) register_11 (.D(out_13), .Q(out_14), .clk(cl), .clr(reset));  // open: en
  Register #(.width(6)) register_12 (.D(out_15), .Q(out_16), .clk(cl), .clr(reset));  // open: en
  Register #(.width(6)) register_13 (.D(out_16), .Q(out_17), .clk(cl), .clr(reset));  // open: en
  Register #(.width(6)) register_14 (.D(out_17), .Q(out_18), .clk(cl), .clr(reset));  // open: en
  Register #(.width(6)) register_15 (.D(out_18), .Q(out_19), .clk(cl), .clr(reset));  // open: en
  Register #(.width(6)) register_16 (.D(out_19), .Q(out_20), .clk(cl), .clr(reset));  // open: en
  Register #(.width(6)) register_17 (.D(out_20), .Q(out_21), .clk(cl), .clr(reset));  // open: en
  Register #(.width(6)) register_18 (.D(out_22), .Q(out_23), .clk(cl), .clr(reset));  // open: en
  Register #(.width(6)) register_19 (.D(out_21), .Q(out_22), .clk(cl), .clr(reset));  // open: en
  Register #(.width(6)) register_20 (.D(out_23), .Q(out_24), .clk(cl), .clr(reset));  // open: en
  Register #(.width(6)) register_21 (.D(out_24), .Q(out_25), .clk(cl), .clr(reset));  // open: en
  Register #(.width(6)) register_22 (.D(out_25), .Q(out_26), .clk(cl), .clr(reset));  // open: en
  Register #(.width(6)) register_23 (.D(out_26), .Q(out_27), .clk(cl), .clr(reset));  // open: en
  Register #(.width(6)) register_24 (.D(out_27), .Q(out_28), .clk(cl), .clr(reset));  // open: en
  Register #(.width(6)) register_25 (.D(out_28), .Q(out_29), .clk(cl), .clr(reset));  // open: en
  Register #(.width(6)) register_26 (.D(out_29), .Q(out_30), .clk(cl), .clr(reset));  // open: en
  Register #(.width(6)) register_27 (.D(out_30), .Q(out_31), .clk(cl), .clr(reset));  // open: en
  Register #(.width(6)) register_28 (.D(out_31), .Q(out_32), .clk(cl), .clr(reset));  // open: en
  Register #(.width(6)) register_29 (.D(out_32), .Q(out_33), .clk(cl), .clr(reset));  // open: en
  Register #(.width(6)) register_30 (.D(out_33), .Q(out_34), .clk(cl), .clr(reset));  // open: en
  Register #(.width(6)) register_31 (.D(out_34), .Q(out_35), .clk(cl), .clr(reset));  // open: en
  Register #(.width(6)) register_32 (.D(out_35), .Q(out_36), .clk(cl), .clr(reset));  // open: en
  Register #(.width(6)) register_33 (.D(out_36), .Q(out_37), .clk(cl), .clr(reset));  // open: en

  // Other names for the same wires on the sheet: r = reset

  // Notes on the sheet:
  //   contents of rom_1 (hex, n*v repeats v):
  //   0 1a 0 1e 4 8 1e 0 12 1e 12 0 1c 2 4 2 1c 0 0 0 1e 2 1e 0 1e 12 1e 0 18 e 18
  //   contents of rom_2 (hex, n*v repeats v):
  //   0 0 12 1a 1e 0 16 1e 1a 0 1e 12 1e 0 2 2 1e 0 0 0 1e 2 1e 0 1e 12 1e 0 18 e 18
  //   contents of rom_3 (hex, n*v repeats v):
  //   0 0 0 c 12 1e 0 14 6*0 1c 2 4 2 1c 0 e 14 e 0 1a 1c 1e 0 c 12 1e
endmodule

// writer
module game_status_writer (
  input  [23:0] game_bus,
  input  clock,
  input  move,
  output [7:0] data,
  output [7:0] addr,
  output reset_out,
  output active
);

  wire and_1_out;
  wire [2:0] counter_2_q;

  Counter #(.width(1), .max('h1)) counter_1 (.Q(active), .clk(move), .clr(reset_out));  // open: load, D, count, carry
  Pull_Resistor pull_resistor_1 (.node(reset_out));
  and and_1 (and_1_out, clock, active);
  Counter #(.width(3), .max('h7)) counter_2 (
    .Q(counter_2_q), .clk(and_1_out), .clr(reset_out));  // open: load, D, count, carry
  Multiplexer #(.select(3), .width(8), .enable("false")) multiplexer_1 (
    .in1(game_bus[23:16]), .in2(game_bus[15:8]), .in3(game_bus[7:0]), .out(data), .sel(counter_2_q));  // open: in0, in4, in5, in6, in7
  Comparator #(.width(3), .mode("unsigned")) comparator_1 (
    .a(counter_2_q), .b(3'b100), .eq(reset_out));  // open: gt, lt
  Multiplexer #(.select(3), .width(8), .enable("false")) multiplexer_2 (
    .in1({8{1'b0}}), .in2(8'h1), .in3(8'h2), .out(addr), .sel(counter_2_q));  // open: in0, in4, in5, in6, in7
endmodule

module byte_selector (
  input  [23:0] game_bus,
  input  I_Osel,
  input  I_O,
  input  [7:0] I_Oadr,
  output [7:0] data
);

  wire and_1_out;
  wire [1:0] game_bus_div_1_out_2, game_bus_div_1_out_3, game_bus_div_1_out_4, game_bus_div_1_out_5,
       game_bus_div_1_out_6, game_bus_div_1_out_7, game_bus_div_1_out_8, game_bus_div_1_out_9,
       game_bus_div_1_out_10, multiplexer_1_out;
  wire [5:5] pull_resistor_1_node;

  game_bus_div game_bus_div_1 (
    .in_1(game_bus), .out_2(game_bus_div_1_out_2), .out_3(game_bus_div_1_out_3),
    .out_4(game_bus_div_1_out_4), .out_5(game_bus_div_1_out_5), .out_6(game_bus_div_1_out_6),
    .out_7(game_bus_div_1_out_7), .out_8(game_bus_div_1_out_8), .out_9(game_bus_div_1_out_9),
    .out_10(game_bus_div_1_out_10));
  Pull_Resistor pull_resistor_1 (.node(pull_resistor_1_node[5]));
  Multiplexer #(.select(4), .width(2), .enable("false")) multiplexer_1 (
    .in0(game_bus_div_1_out_2), .in1(game_bus_div_1_out_3), .in2(game_bus_div_1_out_4),
    .in3(game_bus_div_1_out_5), .in4(game_bus_div_1_out_6), .in5(game_bus_div_1_out_7),
    .in6(game_bus_div_1_out_8), .in7(game_bus_div_1_out_9), .in8(game_bus_div_1_out_10),
    .out(multiplexer_1_out), .sel(I_Oadr[3:0]));  // open: in9, in10, in11, in12, in13, in14, in15
  Multiplexer #(.width(8), .enable("false")) multiplexer_2 (
    .in1({multiplexer_1_out, {6{pull_resistor_1_node[5]}}}), .out(data), .sel(and_1_out));  // open: in0
  and and_1 (and_1_out, I_Osel, I_O);
endmodule

module move_getter (
  input  [7:0] I_Odata,
  input  I_Osel,
  input  I_O,
  output [7:0] data,
  output move
);

  wire not_1_out;

  Multiplexer #(.width(8), .enable("false")) multiplexer_1 (.in1(I_Odata), .out(data), .sel(move));  // open: in0
  and and_1 (move, I_Osel, not_1_out);
  not not_1 (not_1_out, I_O);
endmodule
